# Fritzing sketch Esp32_handonz (saved by Fritzing 0.9.9b)
breadboards: 1

parts:
  R1 = Photocell (LDR) [package=THT]
  R2 = Resistor [tolerance=±5% resistance=220 package="0805 [SMD]"]
  LED1 = smd LED [color="Red (633nm)" package="1206 [SMD]"]
  U2 = LuaNode32 / ESP32 [part_number=ESP32S-PIN30]

nets:
  N1: R1.pin_0, R2.Pin_1, U2.D2
  N2: R1.pin_1, U2.3V3
  N3: R2.Pin_0, LED1.cathode, U2.GND
  N4: LED1.anode, U2.D15

custom parts:
  LuaNode32 / ESP32: New Image for LuaNode32 DOIT ESP32 DEVKIT V1. Base parts from LuaNode32 / ESP32 ESP32 based LuaNode32 by G.Noorlander DOIT Esp32 DevKit v1 (30 pins long, 11 pins width) by Werner Rothschopf (modified by vanepp Dec 2018)
